# Fritzing sketch Breadboard_Wiring (saved by Fritzing 0.9.6b)
breadboards: 2

parts:
  M1 = ESP32 FIREBEETLE IOT V3 [part_number=ESP32_FIREBEETLE]
  J1 = DHT11 basic temperature-humidity sensor [form="♂ (male)" package=THT]
  S1 = Momentary Switch [package=ksa_sealed_tac_switch]
  R1 = Resistor [tolerance=±5% power=0.25 resistance=100 package=THT]
  R4 = Resistor [tolerance=±5% power=0.25 resistance=220 package=THT]
  LED1 = LED - 3mm [color="Blue (430nm)" current=0.030 package="3 mm [THT]"]
  LED2 = LED - 3mm [color="Green (555nm)" current=0.030 package="3 mm [THT]"]
  LED3 = LED - 3mm [color="Red (633nm)" current=0.030 package="3 mm [THT]"]
  R2 = Resistor [tolerance=±5% power=0.25 resistance=22 package=THT]
  R3 = Resistor [tolerance=±5% power=0.25 resistance=22 package=THT]
  Capacitive_Soil_Moisture_Sensor1 = DFRobot Capacitive Soil Moisture Sensor V1.0 [part_number=SEN0193]
  C2 = Capacitor Polarized [package=cpol-radial-100uf-25v]

nets:
  N1: M1.IO25/D2, R3.Pin_1
  N2: M1.IO26/D3, S1.3
  N3: M1.IO27/D4, R2.Pin_1
  N4: M1.IO9/D5, J1.OUT
  N5: M1.IO10/D6, R1.Pin_1
  GND: M1.GND, M1.LIPO-, J1.GND, R4.Pin_0, LED1.cathode, LED2.cathode, LED3.cathode, Capacitive_Soil_Moisture_Sensor1.GND
  3V3: M1.3V3, J1.VCC, S1.1
  VCC: M1.VCC, Capacitive_Soil_Moisture_Sensor1.VCC
  N6: M1.A2/IO34, C2.-
  N7: S1.4, R4.Pin_1
  N8: R1.Pin_0, LED3.anode
  N9: LED1.anode, R3.Pin_0
  N10: LED2.anode, R2.Pin_0
  N11: Capacitive_Soil_Moisture_Sensor1.A, C2.+

custom parts:
  ESP32 FIREBEETLE IOT V3: DFRobot Firebeetle ESP32 IOT Microcontroller V3, 36-Pin ESP32.
  DHT11 basic temperature-humidity sensor: The DHT11 is a basic, ultra low-cost digital temperature and humidity sensor. It uses a capacitive humidity sensor and a thermistor to measure the surrounding air, and spits out a digital signal on the data pin (no analog input pins needed). Its fairly simple to use, but requires careful timing to grab data. The only real downside of this sensor is you can only get new data from it once every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
  DFRobot Capacitive Soil Moisture Sensor V1.0: DFRobot Capacitive Soil Moisture Sensor V1.0 This product measures soil moisture levels by capacitive sensing, rather than resistive sensing like other types of moisture sensor. It is made of a corrosion resistant material giving it a long service life. Insert it into soil and impress your friends with the real-time soil moisture data! The product includes an on-board voltage regulator which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
