# Fritzing sketch Breadboard_Wiring (saved by Fritzing 0.9.6b)
breadboards: 1

parts:
  M1 = ESP32-C3-DevKitC-02 [part_number=ESP32-C3-DevKitC-02]
  LED2 = LED - 3mm [color="Green (555nm)" current=0.030 package="3 mm [THT]"]  # not connected
  DHT11_Module = KY-015 Temperature & Humidity Sensor Module [package="Breakout board"]
  S1 = Momentary Switch [package=ksa_sealed_tac_switch]
  LED1 = LED - 3mm [color="Red (633nm)" current=0.030 package="3 mm [THT]"]
  R4 = Resistor [tolerance=±10% power=0.25 resistance=22 package=THT]
  LED3 = LED - 3mm [color="Blue (430nm)" current=0.030 package="3 mm [THT]"]
  R3 = Resistor [tolerance=±10% power=0.25 resistance=22 package=THT]
  R2 = Resistor [tolerance=±10% power=0.25 resistance=100 package=THT]
  R1 = Resistor [tolerance=±10% power=0.25 resistance=10k package=THT]
  Capacitive_Soil_Moisture_Sensor1 = DFRobot Capacitive Soil Moisture Sensor V1.0 [part_number=SEN0193]
  LED2_2 = LED - 3mm [color="Green (555nm)" current=0.030 package="3 mm [THT]"]

nets:
  VIN: M1.GND#0, M1.GND#1, M1.GND#7, M1.GND#9, M1.GND#14, M1.GND#15, M1.GND#19, M1.GND#24, M1.GND#29, DHT11_Module.Vin, LED1.cathode, LED3.cathode, R1.Pin_0, Capacitive_Soil_Moisture_Sensor1.GND, LED2_2.cathode
  N1: M1.3, R2.Pin_1
  N2: M1.2, R4.Pin_1
  N3: M1.1, R3.Pin_1
  N4: M1.0, S1.1
  3V3: M1.3V3, DHT11_Module.S, Capacitive_Soil_Moisture_Sensor1.VCC
  N5: M1.4, Capacitive_Soil_Moisture_Sensor1.A
  N6: M1.9, DHT11_Module.-
  N7: M1.5V, S1.3
  N8: S1.2, R1.Pin_1
  N9: LED1.anode, R2.Pin_0
  N10: R4.Pin_0, LED3.anode
  N11: R3.Pin_0, LED2_2.anode

notes:
  S1 (Button):
  Press button to send data.
  Emits a low signal when the buttons is depressed.
  Emits a high signal when the buttons is pressed.
  R1 (Button):
  Pull down to ground using a 10K resistor to neutral.
  LED1 (Red):
  On when the device is active, off when it is in a low power state.
  LED2 (Green):
  Flashes then communicating over the network.
  LED3 (Blue):
  User LED can be toggled via the client software.
  R2 (Red LED):
  3.3 - 2.0
  ----------- = 100ohm
  0.013
  R3 (Green LED):
  3.3 - 3.0
  ----------- = 22ohm
  0.0135
  R4 (Blue LED):
  3.3 - 3.0
  ----------- = 22ohm
  0.0135

custom parts:
  ESP32-C3-DevKitC-02: Esp32-C3 DevKitC 02 is one of the development board created by Espressif. It is based on the ESP32 microcontroller that boasts Wifi, Bluetooth, Ethernet and Low Power support all in a single chip. (vanepp) Feb 2021: converted to ESP32-C3-DevKitC-02. This chip is 30pins long (2 x15) and 11 pins width.
  KY-015 Temperature & Humidity Sensor Module: KY-015 temperature and humidity sensor module, provides a low-latency serial interface to measure humidity and temperature.
  DFRobot Capacitive Soil Moisture Sensor V1.0: DFRobot Capacitive Soil Moisture Sensor V1.0 This product measures soil moisture levels by capacitive sensing, rather than resistive sensing like other types of moisture sensor. It is made of a corrosion resistant material giving it a long service life. Insert it into soil and impress your friends with the real-time soil moisture data! The product includes an on-board voltage regulator which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
